# Fritzing sketch BreadBoardLine (saved by Fritzing 0.9.9b)
breadboards: 1

parts:
  U1 = NodeMCU V3.0
  OLED_I2C1 = OLED 128x64 I2C Monochrome Display
  HC-SR04_Sensor_1 = HC-SR04 Ultrasonic Distance Sensor
  J1 = Piezo Speaker

nets:
  N1: U1.D1, OLED_I2C1.SCK
  3V3: U1.3V3, OLED_I2C1.VDD, HC-SR04_Sensor_1.VCC
  GND: U1.GND#6, U1.GND#13, U1.GND#16, U1.GND#33, OLED_I2C1.GND, HC-SR04_Sensor_1.GND, J1.pin1
  N2: U1.D6, J1.pin2
  N3: U1.D8, HC-SR04_Sensor_1.TRIG
  N4: U1.RX, HC-SR04_Sensor_1.ECHO

custom parts:
  NodeMCU V3.0: ESP8266 based NodeMCU
